# Fritzing sketch GeoduinoSchematic (saved by Fritzing 0.9.3b)
breadboards: 1

parts:
  Part1 = Arduino Mega 2560 (Rev3)
  LCD1 = LCD screen
  RHT1 = Humidity and Temperature Sensor RHT03
  R1 = Trimmer Potentiometer [maximum_resistance=10kΩ package=THT]
  R2 = Photocell (LDR) [package=THT]
  R3 = Resistor [tolerance=±5% resistance=1k package=THT]
  S1 = Pushbutton [package="[THT]"]
  S2 = Pushbutton [package="[THT]"]
  R4 = Resistor [tolerance=±5% resistance=10k package=THT]
  R5 = Resistor [tolerance=±5% resistance=10k package=THT]

nets:
  N1: Part1.A0, R2.pin_0, R3.Pin_1
  GND: Part1.GND, LCD1.VSS, LCD1.R/W, LCD1.LED-, RHT1.Data-signal, R1.leg1, R3.Pin_0, R4.Pin_1, R5.Pin_1
  5V: Part1.5V, LCD1.VDD, LCD1.LED+, RHT1.GND_1, R1.leg2, R2.pin_1, S1.Pin_1, S1.Pin_2, S2.Pin_1, S2.Pin_2
  N2: Part1.D2_PWM, LCD1.RS
  N3: Part1.D3_PWM, LCD1.E
  N4: Part1.D4_PWM, LCD1.DB4
  N5: Part1.D5_PWM, LCD1.DB5
  N6: Part1.D6_PWM, LCD1.DB6
  N7: Part1.D7_PWM, LCD1.DB7
  N8: Part1.D22, RHT1.GND_2
  N9: Part1.D24, S1.Pin_3, S1.Pin_4, R5.Pin_0
  N10: Part1.D26, S2.Pin_3, S2.Pin_4, R4.Pin_0
  N11: LCD1.V0, R1.wiper
